# Fritzing sketch module45task1 (saved by Fritzing 0.9.9b)
breadboards: 1

parts:
  U1 = ESP32-38PinWide [part_number=ESP32-38PinWide]
  SM1 = 28BYJ-48 Stepper Motor [part_number=28BYJ-48]
  Driver1 = 28BYJ-48 Driver Module [part_number=ULN2003 package=THT]
  PS1 = prefix0000 [part_number=AC:100V]
  SERVO1 = Tower Pro SG90 servo [part_number=101246]

nets:
  N1: U1.GPIO25, Driver1.IN4
  N2: U1.GPIO26, Driver1.IN3
  N3: U1.GPIO27, Driver1.IN2
  N4: U1.GPIO14, Driver1.IN1
  GND: U1.GND, SERVO1.GND
  N5: U1.GPIO13, SERVO1.Signal
  VIN: U1.VIN, SERVO1.+5V
  N6: SM1.blue-pin, Driver1.blue-pin
  N7: SM1.pink-pin, Driver1.pink-pin
  N8: SM1.yellow-pin, Driver1.yellow-pin
  N9: SM1.orange-pin, Driver1.orange-pin
  N10: SM1.red-pin, Driver1.red-pin
  N11: Driver1.GND, PS1.connector3
  N12: Driver1.Vmotor, PS1.connector0

custom parts:
  ESP32-38PinWide: Generic 38-Pin ESP32 with wide format (only access to one side of pins on a breadboard) based on Stephen Lilley's HiLetgo ESP-WROOM-32 ESP32 ESP-32S Development Board.
  28BYJ-48 Stepper Motor: Unipolar Stepper Motor 28BYJ-48 Top coil - pink & orange Bottom coil - blue & yellow Common rail - red Connector pins: blue - pink - yellow - orange - red
  28BYJ-48 Driver Module: ULN2003 Driver Module for the 28BYJ-48 Unipolar Stepper Motor LED A - Blue wire - Bottom coil left LED B - Pink wire - Top coil left LED C - Yellow wire - Bottom coil right LED D - Orange wire - Top coil right Common rail - red Connector pins: blue - pink - yellow - orange - red Control pins - IN1 to IN4 Power pins - GND & Vmotor (5-12V) On/Off jumper (if removed, power to motor is cut).
  Tower Pro SG90 servo: Original file by John De Cristofaro http://www.adafruit.com/products/1449 Adafruit Feedback Servo (Small) Edited by: e-radionica.com 28/9/2015
